// Logisim project ProcessadorSagui.circ as structural Verilog: 3 circuits, main circuit main
module main (
  output [7:0] out_1,
  output [7:0] out_2,
  output [7:0] out_3,
  output [7:0] out_4,
  output [7:0] out_5,
  output [7:0] out_6
);

  wire and_1_out, Branch, Clk, Jump, MemToReg, MemWrite, UlaSrc, WE;
  wire [3:0] MemControle_data;
  wire [7:0] adder_1_out, adder_2_out, bancor_1_b, bit_extender_1_out, bit_extender_2_out, multiplexer_1_out,
       multiplexer_2_out, multiplexer_3_out, PC_q, ula_1_zero;

  Register PC (.D(multiplexer_1_out), .en(1'b1), .clk(Clk), .Q(PC_q));  // open: clr
  ROM MemInstruc (.addr(PC_q), .data(out_4));
  Multiplexer #(.width(8)) multiplexer_1 (
    .in0(multiplexer_2_out), .in1(bit_extender_1_out), .out(multiplexer_1_out), .sel(Jump));
  Adder adder_1 (.a(8'h1), .b(PC_q), .out(adder_1_out));  // open: cin, cout
  Multiplexer #(.width(8)) multiplexer_2 (
    .in0(adder_1_out), .in1(adder_2_out), .out(multiplexer_2_out), .sel(and_1_out));
  assign bit_extender_1_out = {{4{out_4[3]}}, out_4[3:0]};  // Bit_Extender bit_extender_1
  Adder adder_2 (.a(bit_extender_1_out), .b(adder_1_out), .out(adder_2_out));  // open: cin, cout
  and and_1 (and_1_out, Branch, ula_1_zero[0]);
  ROM #(.addrWidth(4), .dataWidth(10)) MemControle (
    .addr(out_4[7:4]), .data({Jump, Branch, MemToReg, MemWrite, WE, UlaSrc, MemControle_data}));
  assign bit_extender_2_out = {{4{out_4[3]}}, out_4[3:0]};  // Bit_Extender bit_extender_2
  BancoR bancor_1 (
    .WriteEnabled(WE), .WriteValue(out_6), .Register_B(out_4[1:0]), .Register_A(out_4[3:2]), .Clr(1'b0),
    .Clk(Clk), .out_7(out_2), .A(out_5), .B(bancor_1_b));
  Multiplexer #(.width(8)) multiplexer_3 (
    .in0(bancor_1_b), .in1(bit_extender_2_out), .out(multiplexer_3_out), .sel(UlaSrc));
  ULA ula_1 (
    .R0(out_2), .OpCode(MemControle_data), .Register_A(out_5), .Register_B(multiplexer_3_out),
    .Zero(ula_1_zero), .Result(out_1));
  Clock clock_1 (.out(Clk));
  RAM #(.asyncread("true")) ram_1 (.addr(out_1), .we(MemWrite), .oe(MemToReg), .clk(Clk), .din(out_5), .dout(out_3));
  Multiplexer #(.width(8)) multiplexer_4 (.in0(out_1), .in1(out_3), .out(out_6), .sel(MemToReg));

  // Notes on the sheet:
  //   contents of MemInstruc (hex, n*v repeats v):
  //   83 52 30 205*0 41 52 30
  //   Branch
  //   contents of MemControle (hex, n*v repeats v):
  //   100 111 202 213 a4 45 26 37 38 29 2a 2b 2c 2d 2e 2f
  //   Jump
  //   Branch
  //   MemToReg
  //   MemWrite
  //   WE
  //   UlaSrc
  //   UlaControl
endmodule

module BancoR (
  input  WriteEnabled,
  input  [7:0] WriteValue,
  input  [1:0] Register_B,
  input  [1:0] Register_A,
  input  Clr,
  input  Clk,
  output [7:0] out_7,
  output [7:0] A,
  output [7:0] B
);

  wire demultiplexer_1_out0, demultiplexer_1_out1, demultiplexer_1_out2, demultiplexer_1_out3;
  wire [7:0] register_2_q, register_3_q, register_4_q;

  Demultiplexer #(.select(2)) demultiplexer_1 (
    .out0(demultiplexer_1_out0), .out1(demultiplexer_1_out1), .out2(demultiplexer_1_out2),
    .out3(demultiplexer_1_out3), .in(Clk), .sel(Register_A));
  Register register_1 (.D(WriteValue), .en(WriteEnabled), .clk(demultiplexer_1_out0), .Q(out_7), .clr(Clr));
  Register register_2 (.D(WriteValue), .en(WriteEnabled), .clk(demultiplexer_1_out1), .Q(register_2_q), .clr(Clr));
  Register register_3 (.D(WriteValue), .en(WriteEnabled), .clk(demultiplexer_1_out2), .Q(register_3_q), .clr(Clr));
  Register register_4 (.D(WriteValue), .en(WriteEnabled), .clk(demultiplexer_1_out3), .Q(register_4_q), .clr(Clr));
  Multiplexer #(.select(2), .width(8)) multiplexer_1 (
    .in0(out_7), .in1(register_2_q), .in2(register_3_q), .in3(register_4_q), .out(A), .sel(Register_A));
  Multiplexer #(.select(2), .width(8)) multiplexer_2 (
    .in0(out_7), .in1(register_2_q), .in2(register_3_q), .in3(register_4_q), .out(B), .sel(Register_B));
endmodule

module ULA (
  input  [7:0] R0,
  input  [3:0] OpCode,
  input  [7:0] Register_A,
  input  [7:0] Register_B,
  output [7:0] Zero,
  output [7:0] Result
);

  wire comparator_1_eq, comparator_2_eq;
  wire [7:0] adder_1_out, adder_2_out, adder_3_out, and_1_out, bit_extender_1_out, bit_extender_2_out,
       bit_extender_4_out, negator_1_out, or_1_out, shifter_1_out, shifter_2_out, shifter_3_out,
       subtractor_1_out;

  assign bit_extender_1_out = {{4{Register_B[3]}}, Register_B[3:0]};  // Bit_Extender bit_extender_1
  assign bit_extender_2_out = {{4{Register_B[7]}}, Register_B[7:4]};  // Bit_Extender bit_extender_2
  Shifter shifter_1 (.in(bit_extender_2_out), .\dist (3'b100), .out(shifter_1_out));
  Comparator #(.mode("unsigned")) comparator_1 (.a(Register_A), .b({8{1'b0}}), .eq(comparator_1_eq));  // open: gt, lt
  Comparator #(.mode("unsigned")) comparator_2 (.a(Register_A), .b({8{1'b0}}), .eq(comparator_2_eq));  // open: gt, lt
  Adder adder_1 (.a(Register_A), .b(Register_B), .out(adder_1_out));  // open: cin, cout
  Subtractor subtractor_1 (.a(Register_A), .b(Register_B), .out(subtractor_1_out));  // open: bin, bout
  assign and_1_out = Register_A & Register_B;  // AND_Gate and_1, 8 bits wide
  assign or_1_out = Register_A | Register_B;  // OR_Gate or_1, 8 bits wide
  Negator negator_1 (.in(Register_B), .out(negator_1_out));
  Shifter shifter_2 (.in(Register_A), .\dist (Register_B[2:0]), .out(shifter_2_out));
  Shifter #(.shift("lr")) shifter_3 (.in(Register_A), .\dist (Register_B[2:0]), .out(shifter_3_out));
  Adder adder_2 (.a(R0), .b(bit_extender_1_out), .out(adder_2_out));  // open: cin, cout
  Adder adder_3 (.a(R0), .b(shifter_1_out), .out(adder_3_out));  // open: cin, cout
  assign Zero = {{7{comparator_1_eq}}, comparator_1_eq};  // Bit_Extender bit_extender_3
  assign bit_extender_4_out = {{7{comparator_2_eq}}, comparator_2_eq};  // Bit_Extender bit_extender_4
  Multiplexer #(.select(4), .width(8)) multiplexer_1 (
    .in0(Zero), .in1(bit_extender_4_out), .in2(8'h1), .in3(8'h1), .in4(Register_B), .in5(Register_B),
    .in6(Register_B), .in7(adder_3_out), .in8(adder_2_out), .in9(adder_1_out), .in10(subtractor_1_out),
    .in11(and_1_out), .in12(or_1_out), .in13(negator_1_out), .in14(shifter_2_out), .in15(shifter_3_out),
    .out(Result), .sel(OpCode));
endmodule
